# Fritzing sketch switcher (saved by Fritzing 0.9.3b)
circuit board: 8.24488cm x 6.6214cm
breadboards: 1

parts:
  S1 = Pushbutton [package="[THT]"]
  IC1 = IC, DIP package, 10 pins [chip_label=IC part_number=EA2-5TNAG]
  R1 = Resistor [tolerance=±5% resistance=1k package=THT]
  S2 = Pushbutton [package="[THT]"]
  R3 = Resistor [tolerance=±5% resistance=1k package=THT]
  J1 = AVR ISP 6 Pin [package=2x3_lock]
  D1 = Rectifier Diode [part_number=1N4001 package="300 mil [THT]"]
  D2 = Rectifier Diode [part_number=1N4001 package="300 mil [THT]"]
  R5 = Resistor [tolerance=±5% resistance=6.8k package=THT]
  R6 = Resistor [tolerance=±5% resistance=6.8k package=THT]
  R7 = Resistor [tolerance=±5% resistance=6.8k package=THT]
  R8 = Resistor [tolerance=±5% resistance=6.8k package=THT]
  IC3 = IC, DIP package, 16 pins [chip_label=IC part_number=TLP521-4]
  IC4 = IC, DIP package, 10 pins [chip_label=IC part_number=EA2-5TNAG]
  D4 = Rectifier Diode [part_number=1N4001 package="300 mil [THT]"]
  JP11 = Header 1 [package=1x01_offset]
  GND = Header 1 [package=1x01_offset]
  O1GND = Header 1 [package=1x01_offset]
  O1L = Header 1 [package=1x01_offset]
  O1R = Header 1 [package=1x01_offset]
  O2R = Header 1 [package=1x01_offset]
  O2GND = Header 1 [package=1x01_offset]
  O2L = Header 1 [package=1x01_offset]
  I1R = Header 1 [package=1x01_offset]
  I1L = Header 1 [package=1x01_offset]
  I1GND = Header 1 [package=1x01_offset]
  I2L = Header 1 [package=1x01_offset]
  I2GND = Header 1 [package=1x01_offset]
  I2R = Header 1 [package=1x01_offset]
  U2 = atmega168 [package=dip]
  R9 = Resistor [tolerance=±5% resistance=4.7k package=THT]
  D3 = Rectifier Diode [part_number=1N4001 package="300 mil [THT]"]

nets:
  N1: S1.Pin_1, S1.Pin_2, R1.Pin_1, U2.D8
  GND: S1.Pin_3, S1.Pin_4, S2.Pin_3, S2.Pin_4, J1.6, IC3.pin2, IC3.pin4, IC3.pin6, IC3.pin8, IC3.pin9, IC3.pin11, IC3.pin13, IC3.pin15, GND.1, O1GND.1, O2GND.1, I1GND.1, I2GND.1, U2.GND
  5V: IC1.pin1, IC1.pin10, R1.Pin_0, R3.Pin_0, J1.2, D1.cathode, D2.cathode, IC4.pin1, IC4.pin10, D4.cathode, JP11.1, U2.VCC, R9.Pin_0, D3.cathode
  N2: IC1.pin2, I1L.1
  N3: IC1.pin3, IC4.pin3
  N4: IC1.pin4, I2L.1
  N5: IC1.pin5, D1.anode, IC3.pin16
  N6: IC1.pin6, D2.anode, IC3.pin14
  N7: IC1.pin7, I2R.1
  N8: IC1.pin8, IC4.pin8
  N9: IC1.pin9, I1R.1
  N10: S2.Pin_1, S2.Pin_2, R3.Pin_1, U2.D7
  N11: J1.1, U2.D12
  N12: J1.3, U2.D13
  N13: J1.4, U2.D11_(PWM)
  N14: J1.5, U2.RESET, R9.Pin_1
  N15: R5.Pin_0, U2.A5
  N16: R5.Pin_1, IC3.pin1
  N17: R6.Pin_0, U2.A4
  N18: R6.Pin_1, IC3.pin3
  N19: R7.Pin_0, U2.A3
  N20: R7.Pin_1, IC3.pin5
  N21: R8.Pin_0, U2.A2
  N22: R8.Pin_1, IC3.pin7
  N23: IC3.pin10, IC4.pin6, D4.anode
  N24: IC3.pin12, IC4.pin5, D3.anode
  N25: IC4.pin2, O1L.1
  N26: IC4.pin4, O2L.1
  N27: IC4.pin7, O2R.1
  N28: IC4.pin9, O1R.1
